# Fritzing sketch weatherdock_sketch (saved by Fritzing 0.7.10b)
breadboards: 1

parts:
  Arduino1 = Arduino
  U1 = mystery part, 8 pins [chip_label="ENC28J60   _" part_number="ENC28J60 "]
  DC_Power1 = DC Power [voltage=5]
  S1 = Pushbutton [package=THT]
  S2 = Pushbutton [package=THT]
  S3 = Pushbutton [package=THT]
  S4 = Pushbutton [package=THT]
  R1 = Resistor [tolerance=±5% resistance=10k package=THT]
  R2 = Resistor [tolerance=±5% resistance=10k package=THT]
  R3 = Resistor [tolerance=±5% resistance=10k package=THT]
  R4 = Resistor [tolerance=±5% resistance=10k package=THT]
  R5 = Resistor [tolerance=±5% resistance=470 package=THT]
  GLCD_128x1 = 128 x 64 Graphic LCD

nets:
  N1: Arduino1.D13, U1.pin2
  N2: Arduino1.D12, U1.pin3
  N3: Arduino1.D11, U1.pin4
  N4: Arduino1.D10, U1.pin5
  N5: Arduino1.D9, GLCD_128x1.5_R/W
  N6: Arduino1.D8, GLCD_128x1.4_D/I
  N7: Arduino1.D7, S1.leg0, R1.Pin_1
  N8: Arduino1.D6, S2.leg0, R2.Pin_1
  N9: Arduino1.D5, S3.leg0, R3.Pin_1
  N10: Arduino1.D4, S4.leg0, R4.Pin_1
  N11: Arduino1.D3, GLCD_128x1.6_Enable
  N12: Arduino1.D2, R5.Pin_0
  N13: Arduino1.VIN, DC_Power1.V+
  3.3V: U1.pin1
  GND: U1.pin8, R1.Pin_0, R2.Pin_0, R3.Pin_0, R4.Pin_0, GLCD_128x1.1_Vss, GLCD_128x1.20_K(-)
  5V: S1.leg1, S2.leg1, S3.leg1, S4.leg1, GLCD_128x1.2_Vdd
  N14: R5.Pin_1, GLCD_128x1.19_A(+)

notes:
  ENC28J60 Ethernet module with RJ45 connector
  Pull-up buttons
  Serial communication to another Arduino
