# Fritzing sketch homeautomation (saved by Fritzing 0.7.10b)
breadboards: 1

parts:
  Arduino1 = Arduino
  Part1 = Real Time Clock Module - DS1307 RTC Breakout Board
  J1 = Piezo Speaker [part_number="Piezzo speaker"]
  IR1 = TSOP312.., 314.. [package=THT]
  DC_Power1 = DC Power [voltage=5]
  U1 = TLP621 [package=THT]
  LED1 = smd LED [color="Red (633nm)" package="0805 [SMD]"]
  Part2 = Relay T73
  J2 = screw terminal, 3 pins

nets:
  N1: Arduino1.D11, LED1.cathode
  N2: Arduino1.D4, J1.pin2
  N3: Arduino1.D3, IR1.Data
  N4: Arduino1.VIN, DC_Power1.V+
  N5: Arduino1.A4, Part1.SDA
  N6: Arduino1.A5, Part1.SCL
  5V: Part1.5V, IR1.Vs, U1.Pin_1, U1.Pin_4, Part2.C2
  GND: Part1.GND, J1.pin1, IR1.GND, DC_Power1.GND
  N7: U1.Pin_2, LED1.anode
  N8: U1.Pin_3, Part2.C1
  N9: Part2.COM, J2.pin2
  N10: Part2.NO, J2.pin1
  N11: Part2.NC, J2.pin3

notes:
  Simplified 8 - Relay module
  One out of eight relays in the Relay module. Used pins D9, D10 and D11
  Serial communication to another Arduino
  220V in
  Normaly open out
  Normally closed out

custom parts:
  Relay T73: An T73 Mini PCB Relay
