# Fritzing sketch weatherstation_sketch (saved by Fritzing 0.7.10b)
breadboards: 1

parts:
  Arduino1 = Arduino
  Part1 = Barometric Pressure Sensor - BMP085 Breakout
  Part2 = Humidity Sensor - HIH-4030 Breakout
  Part3 = Bluetooth Mate Silver
  DC_Power1 = DC Power [voltage=3.3]
  DC_Power2 = DC Power [voltage=5]  # not connected
  MLX90614_Infrared_Thermometer1 = MLX90614 Infrared Thermometer
  C1 = Ceramic Capacitor [capacitance="100 nF" package="0603 [SMD, multilayer]"]
  U1 = mystery part, 3 pins [chip_label="Hall switch  _" part_number="US5881LUA "]
  R1 = Resistor [tolerance=±5% resistance=10k package=THT]

nets:
  N1: Arduino1.D4, Part3.TX_5V
  N2: Arduino1.D3, U1.pin2
  N3: Arduino1.D1TX, Part3.RX_5V
  N4: Arduino1.VIN, DC_Power1.V+
  N5: Arduino1.A0, Part2.OUT
  N6: Arduino1.A4, Part1.SDA, MLX90614_Infrared_Thermometer1.PWM_/_SDA
  N7: Arduino1.A5, Part1.SCL, MLX90614_Infrared_Thermometer1.SCL_/_Vz
  GND: DC_Power1.GND, MLX90614_Infrared_Thermometer1.VSS, C1.1, U1.pin3
  N8: MLX90614_Infrared_Thermometer1.VDD, C1.0
  3.3V: U1.pin1, R1.Pin_0

custom parts:
  MLX90614 Infrared Thermometer: The MLX90614 is an Infra Red thermometer for non contact temperature measurements. Both the IR sensitive thermopile detector chip and the signal conditioning ASSP are integrated in the same TO-39 can.
